# Fritzing sketch esp32-helios-reg (saved by Fritzing 0.9.4)
perfboards: 5

parts:
  IC1 = 6n137 Optocoupler [package="DIP (Dual Inline) [THT]"]
  IC2 = 6n137 Optocoupler [package="DIP (Dual Inline) [THT]"]
  IC3 = 6n137 Optocoupler [package="DIP (Dual Inline) [THT]"]
  IC4 = 6n137 Optocoupler [package="DIP (Dual Inline) [THT]"]
  R1 = Resistor [tolerance=±5% resistance=330 package=THT]
  R2 = Resistor [tolerance=±5% resistance=330 package=THT]
  R3 = Resistor [tolerance=±5% resistance=330 package=THT]
  R8 = Resistor [tolerance=±5% resistance=1k package=THT]
  R5 = Resistor [tolerance=±5% resistance=1k package=THT]
  R6 = Resistor [tolerance=±5% resistance=1k package=THT]
  R7 = Resistor [tolerance=±5% resistance=1k package=THT]
  C1 = Electrolytic Capacitor [capacitance=100µF package="100 mil [THT, electrolytic]"]
  C2 = Ceramic Capacitor [capacitance=100nF package="100 mil [THT, multilayer]"]
  R4 = Resistor [tolerance=±5% resistance=330 package=THT]
  PWM_D11 = male pin header, 1 pin [form="♂ (male)"]
  PWM_D9 = male pin header, 1 pin [form="♂ (male)"]
  PWM_D6 = male pin header, 1 pin [form="♂ (male)"]
  12V->5V = WMYCONGCONG buck converter
  part = Adafruit ESP32-S3 Feather [part_number=ESP32]
  C3 = Ceramic Capacitor [capacitance=47nF package="100 mil [THT, multilayer]"]
  C4 = Ceramic Capacitor [capacitance=47nF package="100 mil [THT, multilayer]"]
  C5 = Ceramic Capacitor [capacitance=47nF package="100 mil [THT, multilayer]"]
  C6 = Ceramic Capacitor [capacitance=47nF package="100 mil [THT, multilayer]"]
  PWM_D5 = male pin header, 1 pin [form="♂ (male)"]

nets:
  N1: IC1.Vf+, R1.Pin_1
  N2: IC1.Vf-, IC2.Vf-, IC3.Vf-, IC4.Vf-, part.GND
  GND: IC1.GND, IC2.GND, IC3.GND, IC4.GND, C1.-, C2.0, 12V->5V.Pin_3, C3.0, C4.0, C5.0, C6.0
  N3: IC1.Vo, R5.Pin_0
  VCC: IC1.Ve, IC1.Vcc, IC2.Ve, IC2.Vcc, IC3.Ve, IC3.Vcc, IC4.Ve, IC4.Vcc, C1.+, C2.1, 12V->5V.Pin_4, C3.1, C4.1, C5.1, C6.1
  N4: IC2.Vf+, R2.Pin_1
  N5: IC2.Vo, R6.Pin_0
  N6: IC3.Vf+, R3.Pin_1
  N7: IC3.Vo, R7.Pin_0
  N8: IC4.Vf+, R4.Pin_1
  N9: IC4.Vo, R8.Pin_0
  N10: R1.Pin_0, part.D11
  N11: R2.Pin_0, part.D9
  N12: R3.Pin_0, part.D6
  N13: R8.Pin_1, PWM_D5.pin1
  N14: R5.Pin_1, PWM_D11.pin1
  N15: R6.Pin_1, PWM_D9.pin1
  N16: R7.Pin_1, PWM_D6.pin1
  N17: R4.Pin_0, part.D5
  12V: 12V->5V.Pin_2

custom parts:
  6n137 Optocoupler: 6n137 fast Optocoupler. With 8 pins on a 300mil dual inline package (DIP) footprint. Ve is strobe input. Output is inverting.
  WMYCONGCONG buck converter: These amazing little DC-DC converters feature a wide input voltage of 4.5-24V and the output voltage can be set to one of six fixed voltages, or fully variable, just by bridging the relevant solder pads on the back of the PCB..
  Adafruit ESP32-S3 Feather: The ESP32-S3 has arrived in Feather format - and what a great way to get started with this powerful new chip from Espressif! With dual 240 MHz cores, WiFi and BLE support, and native USB, this Feather is great for powering your IoT projects. That's right - it's the new Adafruit ESP32-S3 Feather! With native USB and 8 MB flash, this board will let you upgrade your existing ESP32 projects.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
